# Fritzing sketch smartfarm_ (saved by Fritzing 0.8.7b)
breadboards: 1

parts:
  PS1 = prefix0000 [part_number=S-350-60]  # not connected
  U1 = ESP32-38PinWide [part_number=ESP32-38PinWide]
  U2 = Module 4 Relais 5V [package="Module 4 Relais 5V"]
  F1 = Fan - Ventilador [package=THT]  # not connected
  YF-S201_Flow_Meter1 = YF-S201 Water Flow Meter
  U3 = WS2812 RGB LED strip

nets:
  N1: U1.GPIO25, U2.IN1
  N2: U1.GPIO26, U2.IN2
  GND: U1.GND, U2.GND, YF-S201_Flow_Meter1.GND, U3.GND
  N3: U1.VIN, U2.K1-NF
  N4: U2.K1-NO, YF-S201_Flow_Meter1.VCC
  N5: U2.K2-NO, U3.VCC

notes:
  dcdc converter
  12V/plus
  12V/minus
  5V/plus
  5V/minus
  3V/plus
  3V/minus
  powetadaptor/plus
  poweradaptor/minus
  220V/plus
  220V/minus
  220V/접지

custom parts:
  ESP32-38PinWide: Generic 38-Pin ESP32 with wide format (only access to one side of pins on a breadboard) based on Stephen Lilley's HiLetgo ESP-WROOM-32 ESP32 ESP-32S Development Board.
  Module 4 Relais 5V: Module 4 Relais 5V 4x SPD-06VDC-SD-C
  Fan - Ventilador: Ventilador de 2 pines, se encuentra comunmente en computadoras de escritorio
  YF-S201 Water Flow Meter: The YF-S201 Flow Meter. The input voltage is 5V to 24V (DC).
  WS2812 RGB LED strip: WS2812 strip
